// Logisim project relatorio1.circ as structural Verilog: 1 circuit, main circuit main
module main (
  input  A0,
  input  B0,
  output SOMA,
  output CARRY_OUT
);

  xor xor_1 (SOMA, A0, B0);
  and and_1 (CARRY_OUT, A0, B0);
endmodule
