// Logisim project relatorio1somador completo.circ as structural Verilog: 1 circuit, main circuit main
module main (
  input  A0,
  input  B0,
  input  C0,
  output SOMA,
  output CARRY_OUT
);

  wire and_1_out, and_2_out, xor_1_out;

  xor xor_1 (xor_1_out, A0, B0);
  and and_1 (and_1_out, A0, B0);
  xor xor_2 (SOMA, xor_1_out, C0);
  and and_2 (and_2_out, xor_1_out, C0);
  xor xor_3 (CARRY_OUT, and_2_out, and_1_out);
endmodule
