// Logisim project relatorio3.circ as structural Verilog
module MUX (
  input  A0,
  input  Ci,
  input  B0,
  input  [1:0] in_4,
  output S0,
  output Co
);

  wire adder_1_out, and_1_out, not_1_out, or_1_out;

  and and_1 (and_1_out, A0, B0);
  or or_1 (or_1_out, A0, B0);
  not not_1 (not_1_out, A0);
  Adder #(.width(1)) adder_1 (.a(A0), .b(B0), .out(adder_1_out), .cin(Ci), .cout(Co));
  Multiplexer #(.select(2), .disabled(0), .enable("false")) multiplexer_1 (
    .in0(and_1_out), .in1(or_1_out), .in2(not_1_out), .in3(adder_1_out), .out(S0), .sel(in_4));
endmodule
