// Logisim project relatorio4X4somador.circ as structural Verilog: 9 circuits, main circuit main
module main (
  input  Ci,
  input  B0,
  input  B1,
  input  B2,
  input  B3,
  input  A0,
  input  A1,
  input  A2,
  input  A3,
  output C0,
  output S0,
  output S1,
  output S2,
  output S3
);

  wire DECODIFICADOR_2_a_2, DECODIFICADOR_2_b_2, DECODIFICADOR_2_c_2, DECODIFICADOR_2_d_2, DECODIFICADOR_2_e,
       DECODIFICADOR_2_f, DECODIFICADOR_2_g, DECODIFICADOR_3_a_2, DECODIFICADOR_3_b_2, DECODIFICADOR_3_c_2,
       DECODIFICADOR_3_d_2, DECODIFICADOR_3_e, DECODIFICADOR_3_f, DECODIFICADOR_3_g, DECODIFICADOR_a_2,
       DECODIFICADOR_b_2, DECODIFICADOR_c_2, DECODIFICADOR_d_2, DECODIFICADOR_e, DECODIFICADOR_f,
       DECODIFICADOR_g;

  decodificador DECODIFICADOR (
    .A(B3), .B(B2), .C(B1), .D(B0), .a_2(DECODIFICADOR_a_2), .b_2(DECODIFICADOR_b_2),
    .c_2(DECODIFICADOR_c_2), .d_2(DECODIFICADOR_d_2), .e(DECODIFICADOR_e), .f(DECODIFICADOR_f),
    .g(DECODIFICADOR_g));
  decodificador DECODIFICADOR_2 (
    .A(A3), .B(A2), .C(A1), .D(A0), .a_2(DECODIFICADOR_2_a_2), .b_2(DECODIFICADOR_2_b_2),
    .c_2(DECODIFICADOR_2_c_2), .d_2(DECODIFICADOR_2_d_2), .e(DECODIFICADOR_2_e), .f(DECODIFICADOR_2_f),
    .g(DECODIFICADOR_2_g));
  _7_Segment_Display u_7_segment_display_1 (
    .g(DECODIFICADOR_g), .f(DECODIFICADOR_f), .a(DECODIFICADOR_a_2), .b(DECODIFICADOR_b_2),
    .e(DECODIFICADOR_e), .d(DECODIFICADOR_d_2), .c(DECODIFICADOR_c_2));  // open: dp
  _7_Segment_Display u_7_segment_display_2 (
    .g(DECODIFICADOR_2_g), .f(DECODIFICADOR_2_f), .a(DECODIFICADOR_2_a_2), .b(DECODIFICADOR_2_b_2),
    .e(DECODIFICADOR_2_e), .d(DECODIFICADOR_2_d_2), .c(DECODIFICADOR_2_c_2));  // open: dp
  decodificador DECODIFICADOR_3 (
    .A(S0), .B(S1), .C(S2), .D(S3), .a_2(DECODIFICADOR_3_a_2), .b_2(DECODIFICADOR_3_b_2),
    .c_2(DECODIFICADOR_3_c_2), .d_2(DECODIFICADOR_3_d_2), .e(DECODIFICADOR_3_e), .f(DECODIFICADOR_3_f),
    .g(DECODIFICADOR_3_g));
  _7_Segment_Display u_7_segment_display_3 (
    .g(DECODIFICADOR_3_g), .f(DECODIFICADOR_3_f), .a(DECODIFICADOR_3_a_2), .b(DECODIFICADOR_3_b_2),
    .e(DECODIFICADOR_3_e), .d(DECODIFICADOR_3_d_2), .c(DECODIFICADOR_3_c_2));  // open: dp

  // Notes on the sheet:
  //   74283
endmodule

module decodificador (
  input  A,
  input  B,
  input  C,
  input  D,
  output a_2,
  output b_2,
  output c_2,
  output d_2,
  output e,
  output f,
  output g
);

  wire and_1_out, and_2_out, and_3_out, and_4_out, and_5_out, and_6_out, and_7_out, and_8_out, and_9_out,
       and_10_out, and_11_out, and_12_out, and_13_out, and_14_out, and_15_out, and_16_out, and_17_out,
       and_18_out, and_19_out, and_20_out, and_21_out, and_22_out, and_23_out, and_24_out, and_25_out,
       and_26_out, and_27_out, and_28_out, and_29_out, and_30_out, and_31_out, and_32_out, and_33_out,
       and_34_out, and_35_out, not_1_out, not_2_out, not_3_out, not_4_out, not_5_out, not_6_out, not_7_out,
       not_8_out, not_9_out, not_10_out, not_11_out, not_12_out, not_13_out, not_14_out, not_15_out,
       not_16_out, not_17_out, not_18_out, not_19_out, not_20_out, not_21_out, not_22_out, not_23_out,
       not_24_out, not_25_out, not_26_out, not_27_out, not_28_out, not_29_out, not_30_out, not_31_out,
       not_32_out, not_33_out, not_34_out, not_35_out, not_36_out, not_37_out, not_38_out, not_39_out,
       not_40_out, not_41_out, not_42_out, not_43_out;

  not not_1 (not_1_out, B);
  and and_1 (and_1_out, not_1_out, not_2_out);
  not not_2 (not_2_out, D);
  not not_3 (not_3_out, A);
  and and_2 (and_2_out, not_3_out, C);
  not not_4 (not_4_out, A);
  and and_3 (and_3_out, not_4_out, B, D);
  and and_4 (and_4_out, B, C);
  not not_5 (not_5_out, B);
  and and_5 (and_5_out, A, not_5_out, not_6_out);
  not not_6 (not_6_out, C);
  and and_6 (and_6_out, A, not_7_out);
  not not_7 (not_7_out, D);
  not not_8 (not_8_out, A);
  and and_7 (and_7_out, not_8_out, not_9_out);
  not not_9 (not_9_out, B);
  not not_10 (not_10_out, A);
  not not_11 (not_11_out, C);
  and and_8 (and_8_out, not_10_out, not_11_out, not_12_out);
  not not_12 (not_12_out, D);
  not not_13 (not_13_out, B);
  and and_9 (and_9_out, not_13_out, not_14_out);
  not not_14 (not_14_out, D);
  not not_15 (not_15_out, A);
  and and_10 (and_10_out, not_15_out, C, D);
  not not_16 (not_16_out, C);
  and and_11 (and_11_out, A, not_16_out, D);
  not not_17 (not_17_out, A);
  and and_12 (and_12_out, not_17_out, not_18_out);
  not not_18 (not_18_out, C);
  not not_19 (not_19_out, A);
  and and_13 (and_13_out, not_19_out, D);
  not not_20 (not_20_out, C);
  and and_14 (and_14_out, not_20_out, D);
  not not_21 (not_21_out, A);
  and and_15 (and_15_out, not_21_out, B);
  and and_16 (and_16_out, A, not_22_out);
  not not_22 (not_22_out, B);
  not not_23 (not_23_out, A);
  not not_24 (not_24_out, B);
  and and_17 (and_17_out, not_23_out, not_24_out, not_25_out);
  not not_25 (not_25_out, D);
  not not_26 (not_26_out, B);
  and and_18 (and_18_out, not_26_out, C, D);
  not not_27 (not_27_out, C);
  and and_19 (and_19_out, B, not_27_out, D);
  and and_20 (and_20_out, B, C, not_28_out);
  not not_28 (not_28_out, D);
  and and_21 (and_21_out, A, not_29_out);
  not not_29 (not_29_out, C);
  not not_30 (not_30_out, B);
  and and_22 (and_22_out, not_30_out, not_31_out);
  not not_31 (not_31_out, D);
  and and_23 (and_23_out, C, not_32_out);
  not not_32 (not_32_out, D);
  and and_24 (and_24_out, A, C);
  and and_25 (and_25_out, A, B);
  not not_33 (not_33_out, C);
  and and_26 (and_26_out, not_33_out, not_34_out);
  not not_34 (not_34_out, D);
  not not_35 (not_35_out, A);
  and and_27 (and_27_out, not_35_out, B, not_36_out);
  not not_36 (not_36_out, C);
  and and_28 (and_28_out, B, not_37_out);
  not not_37 (not_37_out, D);
  and and_29 (and_29_out, A, not_38_out);
  not not_38 (not_38_out, B);
  and and_30 (and_30_out, A, C);
  not not_39 (not_39_out, B);
  and and_31 (and_31_out, not_39_out, C);
  and and_32 (and_32_out, C, not_40_out);
  not not_40 (not_40_out, D);
  not not_41 (not_41_out, A);
  and and_33 (and_33_out, not_41_out, B, not_42_out);
  not not_42 (not_42_out, C);
  and and_34 (and_34_out, A, not_43_out);
  not not_43 (not_43_out, B);
  and and_35 (and_35_out, A, D);
  or or_1 (b_2, and_7_out, and_8_out, and_9_out, and_10_out, and_11_out);
  or or_2 (c_2, and_12_out, and_13_out, and_14_out, and_15_out, and_16_out);
  or or_3 (d_2, and_17_out, and_18_out, and_19_out, and_20_out, and_21_out);
  or or_4 (e, and_22_out, and_23_out, and_24_out, and_25_out);
  or or_5 (f, and_26_out, and_27_out, and_28_out, and_29_out, and_30_out);
  or or_6 (g, and_31_out, and_32_out, and_33_out, and_34_out, and_35_out);
  or or_7 (a_2, and_1_out, and_2_out, and_3_out, and_4_out, and_5_out, and_6_out);
endmodule

module somador_completo_1_bit (
  input  Vem1,
  input  A,
  input  B,
  output Soma,
  output Val1
);

  wire and_1_out, and_2_out, xor_1_out;

  xor xor_1 (xor_1_out, A, B);
  and and_1 (and_1_out, A, B);
  or or_1 (Val1, and_1_out, and_2_out);
  xor xor_2 (Soma, Vem1, xor_1_out);
  and and_2 (and_2_out, Vem1, xor_1_out);
endmodule

module multiplicador_4x4 (
  input  A1,
  input  A2,
  input  A4,
  input  A8,
  input  B1,
  input  B2,
  input  B4,
  input  B8,
  output S128,
  output S64,
  output S32,
  output S16,
  output S8,
  output S4,
  output S2,
  output S1
);

  wire and_1_out, and_2_out, and_3_out, and_4_out, and_5_out, and_6_out, and_7_out,
       somador_completo_1_bit_2_val1, somador_completo_1_bit_3_val1, somador_completo_1_bit_4_val1,
       somador_completo_1_bit_5_val1, somador_completo_1_bit_6_val1;

  and and_1 (and_1_out, B4, A8);
  somador_completo_1_bit somador_completo_1_bit_1 (
    .Vem1(1'b0), .A(somador_completo_1_bit_2_val1), .B(and_1_out), .Val1(S128), .Soma(S64));
  buf and_2 (and_2_out, A4);  // AND_Gate
  somador_completo_1_bit somador_completo_1_bit_2 (
    .Vem1(1'b0), .A(somador_completo_1_bit_3_val1), .B(and_2_out), .Val1(somador_completo_1_bit_2_val1),
    .Soma(S32));
  and and_3 (and_3_out, B4, A2);
  somador_completo_1_bit somador_completo_1_bit_3 (
    .Vem1(1'b0), .A(somador_completo_1_bit_4_val1), .B(and_3_out), .Val1(somador_completo_1_bit_3_val1),
    .Soma(S16));
  and and_4 (and_4_out, B2, A4);
  somador_completo_1_bit somador_completo_1_bit_4 (
    .Vem1(1'b0), .A(somador_completo_1_bit_5_val1), .B(and_4_out), .Val1(somador_completo_1_bit_4_val1),
    .Soma(S8));
  and and_5 (and_5_out, B2, A2);
  somador_completo_1_bit somador_completo_1_bit_5 (
    .Vem1(1'b0), .A(somador_completo_1_bit_6_val1), .B(and_5_out), .Val1(somador_completo_1_bit_5_val1),
    .Soma(S4));
  and and_6 (and_6_out, B2, A1);
  and and_7 (and_7_out, B1, A2);
  somador_completo_1_bit somador_completo_1_bit_6 (
    .Vem1(1'b0), .A(and_7_out), .B(and_6_out), .Val1(somador_completo_1_bit_6_val1), .Soma(S2));
  and and_8 (S1, B1, A1);
endmodule

module v2_4x4 (
  input  A1,
  input  A2,
  input  A4,
  input  A8,
  input  B1,
  input  B2,
  input  B4,
  input  B8,
  output _32,
  output _128,
  output _64,
  output _16,
  output _8,
  output _4,
  output _2,
  output _1
);

  wire and_1_out, and_2_out, and_3_out, and_4_out, and_5_out, and_6_out, and_7_out, and_8_out, and_9_out,
       and_10_out, and_11_out, and_12_out, and_13_out, and_14_out, and_15_out, and_16_out,
       somador_completo_1_bit_2_soma, somador_completo_1_bit_2_val1, somador_completo_1_bit_3_val1,
       somador_completo_1_bit_4_soma, somador_completo_1_bit_4_val1, somador_completo_1_bit_5_val1,
       somador_completo_1_bit_6_soma, somador_completo_1_bit_6_val1, somador_completo_1_bit_7_soma,
       somador_completo_1_bit_7_val1, somador_completo_1_bit_8_val1, somador_completo_1_bit_9_soma,
       somador_completo_1_bit_9_val1, somador_completo_1_bit_10_soma, somador_completo_1_bit_10_val1,
       somador_completo_1_bit_11_val1, somador_completo_1_bit_12_val1;

  and and_1 (and_1_out, B8, A8);
  somador_completo_1_bit somador_completo_1_bit_1 (
    .Vem1(somador_completo_1_bit_3_val1), .A(somador_completo_1_bit_2_val1), .B(and_1_out), .Val1(_128),
    .Soma(_64));
  and and_2 (and_2_out, B8, A4);
  and and_3 (and_3_out, B4, A8);
  somador_completo_1_bit somador_completo_1_bit_2 (
    .Vem1(somador_completo_1_bit_4_val1), .A(and_3_out), .B(and_2_out), .Val1(somador_completo_1_bit_2_val1),
    .Soma(somador_completo_1_bit_2_soma));
  somador_completo_1_bit somador_completo_1_bit_3 (
    .Vem1(somador_completo_1_bit_5_val1), .A(somador_completo_1_bit_2_soma),
    .B(somador_completo_1_bit_6_val1), .Val1(somador_completo_1_bit_3_val1), .Soma(_32));
  and and_4 (and_4_out, B8, A2);
  somador_completo_1_bit somador_completo_1_bit_4 (
    .Vem1(1'b0), .A(and_5_out), .B(and_4_out), .Val1(somador_completo_1_bit_4_val1),
    .Soma(somador_completo_1_bit_4_soma));
  and and_5 (and_5_out, B4, A4);
  somador_completo_1_bit somador_completo_1_bit_5 (
    .Vem1(somador_completo_1_bit_8_val1), .A(somador_completo_1_bit_6_soma),
    .B(somador_completo_1_bit_4_soma), .Val1(somador_completo_1_bit_5_val1), .Soma(_16));
  and and_6 (and_6_out, B2, A8);
  somador_completo_1_bit somador_completo_1_bit_6 (
    .Vem1(somador_completo_1_bit_7_val1), .A(somador_completo_1_bit_9_val1), .B(and_6_out),
    .Val1(somador_completo_1_bit_6_val1), .Soma(somador_completo_1_bit_6_soma));
  and and_7 (and_7_out, B8, A1);
  somador_completo_1_bit somador_completo_1_bit_7 (
    .Vem1(1'b0), .A(and_8_out), .B(and_7_out), .Val1(somador_completo_1_bit_7_val1),
    .Soma(somador_completo_1_bit_7_soma));
  and and_8 (and_8_out, B4, A2);
  somador_completo_1_bit somador_completo_1_bit_8 (
    .Vem1(somador_completo_1_bit_11_val1), .A(somador_completo_1_bit_9_soma),
    .B(somador_completo_1_bit_7_soma), .Val1(somador_completo_1_bit_8_val1), .Soma(_8));
  and and_9 (and_9_out, B2, A4);
  and and_10 (and_10_out, B1, A8);
  somador_completo_1_bit somador_completo_1_bit_9 (
    .Vem1(somador_completo_1_bit_10_val1), .A(and_10_out), .B(and_9_out),
    .Val1(somador_completo_1_bit_9_val1), .Soma(somador_completo_1_bit_9_soma));
  and and_11 (and_11_out, B4, A1);
  somador_completo_1_bit somador_completo_1_bit_10 (
    .Vem1(1'b0), .A(and_12_out), .B(and_11_out), .Val1(somador_completo_1_bit_10_val1),
    .Soma(somador_completo_1_bit_10_soma));
  and and_12 (and_12_out, B2, A2);
  somador_completo_1_bit somador_completo_1_bit_11 (
    .Vem1(somador_completo_1_bit_12_val1), .A(and_13_out), .B(somador_completo_1_bit_10_soma),
    .Val1(somador_completo_1_bit_11_val1), .Soma(_4));
  and and_13 (and_13_out, B1, A4);
  and and_14 (and_14_out, B2, A1);
  somador_completo_1_bit somador_completo_1_bit_12 (
    .Vem1(1'b0), .A(and_15_out), .B(and_14_out), .Val1(somador_completo_1_bit_12_val1), .Soma(_2));
  and and_15 (and_15_out, B1, A2);
  and and_16 (and_16_out, B1, A1);
  somador_completo_1_bit somador_completo_1_bit_13 (.Vem1(1'b0), .A(and_16_out), .B(1'b0), .Soma(_1));  // open: Val1
endmodule

module ULA_74181 (
  input  [3:0] A,
  input  [3:0] B,
  input  [3:0] in_3,
  output [3:0] F
);

  wire [3:0] and_1_out, and_2_out, and_3_out, nand_1_out, nor_1_out, not_1_out, not_2_out, not_3_out,
       not_4_out, not_5_out, not_6_out, or_1_out, or_2_out, or_3_out, xnor_1_out, xor_1_out;

  assign not_1_out = ~A;  // NOT_Gate not_1, 4 bits wide
  assign not_2_out = ~B;  // NOT_Gate not_2, 4 bits wide
  assign xor_1_out = A ^ B;  // XOR_Gate xor_1, 4 bits wide
  assign and_1_out = A & not_3_out;  // AND_Gate and_1, 4 bits wide
  assign not_3_out = ~B;  // NOT_Gate not_3, 4 bits wide
  assign not_4_out = ~A;  // NOT_Gate not_4, 4 bits wide
  assign or_1_out = not_4_out | B;  // OR_Gate or_1, 4 bits wide
  assign xnor_1_out = ~(A ^ B);  // XNOR_Gate xnor_1, 4 bits wide
  assign and_2_out = A & B;  // AND_Gate and_2, 4 bits wide
  assign or_2_out = A | not_5_out;  // OR_Gate or_2, 4 bits wide
  assign not_5_out = ~B;  // NOT_Gate not_5, 4 bits wide
  assign or_3_out = A | B;  // OR_Gate or_3, 4 bits wide
  assign and_3_out = not_1_out & B;  // AND_Gate and_3, 4 bits wide
  assign nand_1_out = ~(A & B);  // NAND_Gate nand_1, 4 bits wide
  assign not_6_out = ~A;  // NOT_Gate not_6, 4 bits wide
  assign nor_1_out = ~(A | B);  // NOR_Gate nor_1, 4 bits wide
  Multiplexer #(.select(4), .width(4), .enable("false")) multiplexer_1 (
    .in0(not_6_out), .in1(nor_1_out), .in2(and_3_out), .in3(4'b0000), .in4(nand_1_out), .in5(not_2_out),
    .in6(xor_1_out), .in7(and_1_out), .in8(or_1_out), .in9(xnor_1_out), .in10(B), .in11(and_2_out),
    .in12(4'b1111), .in13(or_2_out), .in14(or_3_out), .in15(A), .out(F), .sel(in_3));
endmodule

module test (
  input  A1,
  input  A2,
  input  A4,
  input  A8,
  input  B1,
  input  B2,
  input  B4,
  input  B8,
  output _32,
  output _128,
  output _64,
  output _16,
  output _8,
  output _4,
  output _2,
  output _1
);

  wire and_1_out, and_2_out, and_3_out, and_4_out, and_5_out, and_6_out, and_7_out, and_8_out, and_9_out,
       and_10_out, and_11_out, and_12_out, and_13_out, and_14_out, and_15_out, and_16_out,
       somador_completo_1_bit_2_soma, somador_completo_1_bit_2_val1, somador_completo_1_bit_3_val1,
       somador_completo_1_bit_4_soma, somador_completo_1_bit_4_val1, somador_completo_1_bit_5_val1,
       somador_completo_1_bit_6_soma, somador_completo_1_bit_6_val1, somador_completo_1_bit_7_soma,
       somador_completo_1_bit_7_val1, somador_completo_1_bit_8_val1, somador_completo_1_bit_9_soma,
       somador_completo_1_bit_9_val1, somador_completo_1_bit_10_soma, somador_completo_1_bit_10_val1,
       somador_completo_1_bit_11_val1, somador_completo_1_bit_12_val1;

  and and_1 (and_1_out, B8, A8);
  somador_completo_1_bit somador_completo_1_bit_1 (
    .Vem1(somador_completo_1_bit_3_val1), .A(somador_completo_1_bit_2_val1), .B(and_1_out), .Val1(_128),
    .Soma(_64));
  and and_2 (and_2_out, B8, A4);
  and and_3 (and_3_out, B4, A8);
  somador_completo_1_bit somador_completo_1_bit_2 (
    .Vem1(somador_completo_1_bit_4_val1), .A(and_3_out), .B(and_2_out), .Val1(somador_completo_1_bit_2_val1),
    .Soma(somador_completo_1_bit_2_soma));
  somador_completo_1_bit somador_completo_1_bit_3 (
    .Vem1(somador_completo_1_bit_5_val1), .A(somador_completo_1_bit_2_soma),
    .B(somador_completo_1_bit_6_val1), .Val1(somador_completo_1_bit_3_val1), .Soma(_32));
  and and_4 (and_4_out, B8, A2);
  somador_completo_1_bit somador_completo_1_bit_4 (
    .Vem1(1'b0), .A(and_5_out), .B(and_4_out), .Val1(somador_completo_1_bit_4_val1),
    .Soma(somador_completo_1_bit_4_soma));
  and and_5 (and_5_out, B4, A4);
  somador_completo_1_bit somador_completo_1_bit_5 (
    .Vem1(somador_completo_1_bit_8_val1), .A(somador_completo_1_bit_6_soma),
    .B(somador_completo_1_bit_4_soma), .Val1(somador_completo_1_bit_5_val1), .Soma(_16));
  and and_6 (and_6_out, B2, A8);
  somador_completo_1_bit somador_completo_1_bit_6 (
    .Vem1(somador_completo_1_bit_7_val1), .A(1'b0), .B(and_6_out), .Val1(somador_completo_1_bit_6_val1),
    .Soma(somador_completo_1_bit_6_soma));
  and and_7 (and_7_out, B8, A1);
  somador_completo_1_bit somador_completo_1_bit_7 (
    .Vem1(somador_completo_1_bit_9_val1), .A(and_8_out), .B(and_7_out), .Val1(somador_completo_1_bit_7_val1),
    .Soma(somador_completo_1_bit_7_soma));
  and and_8 (and_8_out, B4, A2);
  and and_9 (and_9_out, B2, A4);
  somador_completo_1_bit somador_completo_1_bit_8 (
    .Vem1(somador_completo_1_bit_11_val1), .A(somador_completo_1_bit_9_soma),
    .B(somador_completo_1_bit_7_soma), .Val1(somador_completo_1_bit_8_val1), .Soma(_8));
  and and_10 (and_10_out, B1, A8);
  somador_completo_1_bit somador_completo_1_bit_9 (
    .Vem1(somador_completo_1_bit_10_val1), .A(and_10_out), .B(and_9_out),
    .Val1(somador_completo_1_bit_9_val1), .Soma(somador_completo_1_bit_9_soma));
  and and_11 (and_11_out, B4, A1);
  somador_completo_1_bit somador_completo_1_bit_10 (
    .Vem1(1'b0), .A(and_12_out), .B(and_11_out), .Val1(somador_completo_1_bit_10_val1),
    .Soma(somador_completo_1_bit_10_soma));
  and and_12 (and_12_out, B2, A2);
  somador_completo_1_bit somador_completo_1_bit_11 (
    .Vem1(somador_completo_1_bit_12_val1), .A(and_13_out), .B(somador_completo_1_bit_10_soma),
    .Val1(somador_completo_1_bit_11_val1), .Soma(_4));
  and and_13 (and_13_out, B1, A4);
  and and_14 (and_14_out, B2, A1);
  somador_completo_1_bit somador_completo_1_bit_12 (
    .Vem1(1'b0), .A(and_15_out), .B(and_14_out), .Val1(somador_completo_1_bit_12_val1), .Soma(_2));
  and and_15 (and_15_out, B1, A2);
  and and_16 (and_16_out, B1, A1);
  somador_completo_1_bit somador_completo_1_bit_13 (.Vem1(1'b0), .A(and_16_out), .B(1'b0), .Soma(_1));  // open: Val1
endmodule

module test2 (
  input  A1,
  input  A2,
  input  A4,
  input  A8,
  input  B1,
  input  B2,
  input  B4,
  input  B8,
  output _32,
  output _128,
  output _64,
  output _16,
  output _8,
  output _4,
  output _2,
  output _1
);

  wire and_1_out, and_2_out, and_3_out, and_4_out, and_5_out, and_6_out, and_7_out, and_8_out, and_9_out,
       and_10_out, and_11_out, and_12_out, and_13_out, and_14_out, and_15_out, and_16_out,
       somador_completo_1_bit_2_soma, somador_completo_1_bit_2_val1, somador_completo_1_bit_3_val1,
       somador_completo_1_bit_4_soma, somador_completo_1_bit_4_val1, somador_completo_1_bit_5_val1,
       somador_completo_1_bit_6_soma, somador_completo_1_bit_6_val1, somador_completo_1_bit_7_soma,
       somador_completo_1_bit_7_val1, somador_completo_1_bit_8_val1, somador_completo_1_bit_9_soma,
       somador_completo_1_bit_9_val1, somador_completo_1_bit_10_soma, somador_completo_1_bit_10_val1,
       somador_completo_1_bit_11_val1, somador_completo_1_bit_12_val1;

  and and_1 (and_1_out, B8, A8);
  somador_completo_1_bit somador_completo_1_bit_1 (
    .Vem1(somador_completo_1_bit_3_val1), .A(somador_completo_1_bit_2_val1), .B(and_1_out), .Val1(_128),
    .Soma(_64));
  and and_2 (and_2_out, B8, A4);
  and and_3 (and_3_out, B4, A8);
  somador_completo_1_bit somador_completo_1_bit_2 (
    .Vem1(somador_completo_1_bit_4_val1), .A(and_3_out), .B(and_2_out), .Val1(somador_completo_1_bit_2_val1),
    .Soma(somador_completo_1_bit_2_soma));
  somador_completo_1_bit somador_completo_1_bit_3 (
    .Vem1(somador_completo_1_bit_5_val1), .A(somador_completo_1_bit_2_soma),
    .B(somador_completo_1_bit_6_val1), .Val1(somador_completo_1_bit_3_val1), .Soma(_32));
  and and_4 (and_4_out, B8, A2);
  somador_completo_1_bit somador_completo_1_bit_4 (
    .Vem1(1'b0), .A(and_5_out), .B(and_4_out), .Val1(somador_completo_1_bit_4_val1),
    .Soma(somador_completo_1_bit_4_soma));
  and and_5 (and_5_out, B4, A4);
  somador_completo_1_bit somador_completo_1_bit_5 (
    .Vem1(somador_completo_1_bit_8_val1), .A(somador_completo_1_bit_6_soma),
    .B(somador_completo_1_bit_4_soma), .Val1(somador_completo_1_bit_5_val1), .Soma(_16));
  and and_6 (and_6_out, B2, A8);
  somador_completo_1_bit somador_completo_1_bit_6 (
    .Vem1(somador_completo_1_bit_7_val1), .A(somador_completo_1_bit_9_val1), .B(and_6_out),
    .Val1(somador_completo_1_bit_6_val1), .Soma(somador_completo_1_bit_6_soma));
  and and_7 (and_7_out, B8, A1);
  somador_completo_1_bit somador_completo_1_bit_7 (
    .Vem1(1'b0), .A(and_8_out), .B(and_7_out), .Val1(somador_completo_1_bit_7_val1),
    .Soma(somador_completo_1_bit_7_soma));
  and and_8 (and_8_out, B4, A2);
  somador_completo_1_bit somador_completo_1_bit_8 (
    .Vem1(somador_completo_1_bit_11_val1), .A(somador_completo_1_bit_9_soma),
    .B(somador_completo_1_bit_7_soma), .Val1(somador_completo_1_bit_8_val1), .Soma(_8));
  and and_9 (and_9_out, B2, A4);
  and and_10 (and_10_out, B1, A8);
  somador_completo_1_bit somador_completo_1_bit_9 (
    .Vem1(somador_completo_1_bit_10_val1), .A(and_10_out), .B(and_9_out),
    .Val1(somador_completo_1_bit_9_val1), .Soma(somador_completo_1_bit_9_soma));
  and and_11 (and_11_out, B4, A1);
  somador_completo_1_bit somador_completo_1_bit_10 (
    .Vem1(1'b0), .A(and_12_out), .B(and_11_out), .Val1(somador_completo_1_bit_10_val1),
    .Soma(somador_completo_1_bit_10_soma));
  and and_12 (and_12_out, B2, A2);
  somador_completo_1_bit somador_completo_1_bit_11 (
    .Vem1(somador_completo_1_bit_12_val1), .A(and_13_out), .B(somador_completo_1_bit_10_soma),
    .Val1(somador_completo_1_bit_11_val1), .Soma(_4));
  and and_13 (and_13_out, B1, A4);
  and and_14 (and_14_out, B2, A1);
  somador_completo_1_bit somador_completo_1_bit_12 (
    .Vem1(1'b0), .A(and_15_out), .B(and_14_out), .Val1(somador_completo_1_bit_12_val1), .Soma(_2));
  and and_15 (and_15_out, B1, A2);
  and and_16 (and_16_out, B1, A1);
  somador_completo_1_bit somador_completo_1_bit_13 (.Vem1(1'b0), .A(and_16_out), .B(1'b0), .Soma(_1));  // open: Val1
endmodule

module principal (
  input  A1,
  input  A2,
  input  A4,
  input  A8,
  input  B1,
  input  B2,
  input  B4,
  input  B8,
  output _1,
  output _2,
  output _4,
  output _8,
  output _16,
  output _32,
  output _64,
  output _128
);

  v2_4x4 v2_4x4_1 (
    .A1(A1), .A2(A2), .A4(A4), .A8(A8), .B1(B1), .B2(B2), .B4(B4), .B8(B8), ._128(_128), ._64(_64),
    ._32(_32), ._16(_16), ._8(_8), ._4(_4), ._2(_2), ._1(_1));
endmodule
