// Logisim project relatorio8X8somador.circ as structural Verilog: 4 circuits, main circuit main
module main (
  input  Ci,
  input  B0,
  input  B1,
  input  B2,
  input  B3,
  input  A0,
  input  A1,
  input  A2,
  input  A3,
  output C0,
  output S0,
  output S1,
  output S2,
  output S3
);

  wire DECODIFICADOR_2_a_2, DECODIFICADOR_2_b_2, DECODIFICADOR_2_c_2, DECODIFICADOR_2_d_2, DECODIFICADOR_2_e,
       DECODIFICADOR_2_f, DECODIFICADOR_2_g, DECODIFICADOR_3_a_2, DECODIFICADOR_3_b_2, DECODIFICADOR_3_c_2,
       DECODIFICADOR_3_d_2, DECODIFICADOR_3_e, DECODIFICADOR_3_f, DECODIFICADOR_3_g, DECODIFICADOR_a_2,
       DECODIFICADOR_b_2, DECODIFICADOR_c_2, DECODIFICADOR_d_2, DECODIFICADOR_e, DECODIFICADOR_f,
       DECODIFICADOR_g;

  decodificador DECODIFICADOR (
    .A(B3), .B(B2), .C(B1), .D(B0), .a_2(DECODIFICADOR_a_2), .b_2(DECODIFICADOR_b_2),
    .c_2(DECODIFICADOR_c_2), .d_2(DECODIFICADOR_d_2), .e(DECODIFICADOR_e), .f(DECODIFICADOR_f),
    .g(DECODIFICADOR_g));
  decodificador DECODIFICADOR_2 (
    .A(A3), .B(A2), .C(A1), .D(A0), .a_2(DECODIFICADOR_2_a_2), .b_2(DECODIFICADOR_2_b_2),
    .c_2(DECODIFICADOR_2_c_2), .d_2(DECODIFICADOR_2_d_2), .e(DECODIFICADOR_2_e), .f(DECODIFICADOR_2_f),
    .g(DECODIFICADOR_2_g));
  _7_Segment_Display u_7_segment_display_1 (
    .g(DECODIFICADOR_g), .f(DECODIFICADOR_f), .a(DECODIFICADOR_a_2), .b(DECODIFICADOR_b_2),
    .e(DECODIFICADOR_e), .d(DECODIFICADOR_d_2), .c(DECODIFICADOR_c_2));  // open: dp
  _7_Segment_Display u_7_segment_display_2 (
    .g(DECODIFICADOR_2_g), .f(DECODIFICADOR_2_f), .a(DECODIFICADOR_2_a_2), .b(DECODIFICADOR_2_b_2),
    .e(DECODIFICADOR_2_e), .d(DECODIFICADOR_2_d_2), .c(DECODIFICADOR_2_c_2));  // open: dp
  decodificador DECODIFICADOR_3 (
    .A(S0), .B(S1), .C(S2), .D(S3), .a_2(DECODIFICADOR_3_a_2), .b_2(DECODIFICADOR_3_b_2),
    .c_2(DECODIFICADOR_3_c_2), .d_2(DECODIFICADOR_3_d_2), .e(DECODIFICADOR_3_e), .f(DECODIFICADOR_3_f),
    .g(DECODIFICADOR_3_g));
  _7_Segment_Display u_7_segment_display_3 (
    .g(DECODIFICADOR_3_g), .f(DECODIFICADOR_3_f), .a(DECODIFICADOR_3_a_2), .b(DECODIFICADOR_3_b_2),
    .e(DECODIFICADOR_3_e), .d(DECODIFICADOR_3_d_2), .c(DECODIFICADOR_3_c_2));  // open: dp

  // Notes on the sheet:
  //   74283
endmodule

module decodificador (
  input  A,
  input  B,
  input  C,
  input  D,
  output a_2,
  output b_2,
  output c_2,
  output d_2,
  output e,
  output f,
  output g
);

  wire and_1_out, and_2_out, and_3_out, and_4_out, and_5_out, and_6_out, and_7_out, and_8_out, and_9_out,
       and_10_out, and_11_out, and_12_out, and_13_out, and_14_out, and_15_out, and_16_out, and_17_out,
       and_18_out, and_19_out, and_20_out, and_21_out, and_22_out, and_23_out, and_24_out, and_25_out,
       and_26_out, and_27_out, and_28_out, and_29_out, and_30_out, and_31_out, and_32_out, and_33_out,
       and_34_out, and_35_out, not_1_out, not_2_out, not_3_out, not_4_out, not_5_out, not_6_out, not_7_out,
       not_8_out, not_9_out, not_10_out, not_11_out, not_12_out, not_13_out, not_14_out, not_15_out,
       not_16_out, not_17_out, not_18_out, not_19_out, not_20_out, not_21_out, not_22_out, not_23_out,
       not_24_out, not_25_out, not_26_out, not_27_out, not_28_out, not_29_out, not_30_out, not_31_out,
       not_32_out, not_33_out, not_34_out, not_35_out, not_36_out, not_37_out, not_38_out, not_39_out,
       not_40_out, not_41_out, not_42_out, not_43_out;

  not not_1 (not_1_out, B);
  and and_1 (and_1_out, not_1_out, not_2_out);
  not not_2 (not_2_out, D);
  not not_3 (not_3_out, A);
  and and_2 (and_2_out, not_3_out, C);
  not not_4 (not_4_out, A);
  and and_3 (and_3_out, not_4_out, B, D);
  and and_4 (and_4_out, B, C);
  not not_5 (not_5_out, B);
  and and_5 (and_5_out, A, not_5_out, not_6_out);
  not not_6 (not_6_out, C);
  and and_6 (and_6_out, A, not_7_out);
  not not_7 (not_7_out, D);
  not not_8 (not_8_out, A);
  and and_7 (and_7_out, not_8_out, not_9_out);
  not not_9 (not_9_out, B);
  not not_10 (not_10_out, A);
  and and_8 (and_8_out, not_10_out, not_11_out, not_12_out);
  not not_11 (not_11_out, C);
  not not_12 (not_12_out, D);
  not not_13 (not_13_out, B);
  and and_9 (and_9_out, not_13_out, not_14_out);
  not not_14 (not_14_out, D);
  not not_15 (not_15_out, A);
  and and_10 (and_10_out, not_15_out, C, D);
  and and_11 (and_11_out, A, not_16_out, D);
  not not_16 (not_16_out, C);
  not not_17 (not_17_out, A);
  and and_12 (and_12_out, not_17_out, not_18_out);
  not not_18 (not_18_out, C);
  not not_19 (not_19_out, A);
  and and_13 (and_13_out, not_19_out, D);
  not not_20 (not_20_out, C);
  and and_14 (and_14_out, not_20_out, D);
  not not_21 (not_21_out, A);
  and and_15 (and_15_out, not_21_out, B);
  and and_16 (and_16_out, A, not_22_out);
  not not_22 (not_22_out, B);
  not not_23 (not_23_out, A);
  and and_17 (and_17_out, not_23_out, not_24_out, not_25_out);
  not not_24 (not_24_out, B);
  not not_25 (not_25_out, D);
  not not_26 (not_26_out, B);
  and and_18 (and_18_out, not_26_out, C, D);
  not not_27 (not_27_out, C);
  and and_19 (and_19_out, B, not_27_out, D);
  and and_20 (and_20_out, B, C, not_28_out);
  not not_28 (not_28_out, D);
  and and_21 (and_21_out, A, not_29_out);
  not not_29 (not_29_out, C);
  not not_30 (not_30_out, B);
  and and_22 (and_22_out, not_30_out, not_31_out);
  not not_31 (not_31_out, D);
  and and_23 (and_23_out, C, not_32_out);
  not not_32 (not_32_out, D);
  and and_24 (and_24_out, A, C);
  and and_25 (and_25_out, A, B);
  not not_33 (not_33_out, C);
  and and_26 (and_26_out, not_33_out, not_34_out);
  not not_34 (not_34_out, D);
  not not_35 (not_35_out, A);
  and and_27 (and_27_out, not_35_out, B, not_36_out);
  not not_36 (not_36_out, C);
  and and_28 (and_28_out, B, not_37_out);
  not not_37 (not_37_out, D);
  and and_29 (and_29_out, A, not_38_out);
  not not_38 (not_38_out, B);
  and and_30 (and_30_out, A, C);
  not not_39 (not_39_out, B);
  and and_31 (and_31_out, not_39_out, C);
  and and_32 (and_32_out, C, not_40_out);
  not not_40 (not_40_out, D);
  not not_41 (not_41_out, A);
  and and_33 (and_33_out, not_41_out, B, not_42_out);
  not not_42 (not_42_out, C);
  and and_34 (and_34_out, A, not_43_out);
  not not_43 (not_43_out, B);
  and and_35 (and_35_out, A, D);
  or or_1 (b_2, and_7_out, and_8_out, and_9_out, and_10_out, and_11_out);
  or or_2 (c_2, and_12_out, and_13_out, and_14_out, and_15_out, and_16_out);
  or or_3 (d_2, and_17_out, and_18_out, and_19_out, and_20_out, and_21_out);
  or or_4 (e, and_22_out, and_23_out, and_24_out, and_25_out);
  or or_5 (f, and_26_out, and_27_out, and_28_out, and_29_out, and_30_out);
  or or_6 (g, and_31_out, and_32_out, and_33_out, and_34_out, and_35_out);
  or or_7 (a_2, and_1_out, and_2_out, and_3_out, and_4_out, and_5_out, and_6_out);
endmodule

module somador_completo_1_bit (
  input  Vem1,
  input  A,
  input  B,
  output Soma,
  output Val1
);

  wire and_1_out, and_2_out, xor_1_out;

  xor xor_1 (xor_1_out, A, B);
  and and_1 (and_1_out, A, B);
  or or_1 (Val1, and_1_out, and_2_out);
  xor xor_2 (Soma, Vem1, xor_1_out);
  and and_2 (and_2_out, Vem1, xor_1_out);
endmodule

module multiplicador_4x4 (
  input  A1,
  input  A2,
  input  A3,
  input  A4,
  input  B1,
  input  B2,
  input  B3,
  input  B4,
  output S32768,
  output S16384,
  output S8192,
  output S4096,
  output S2048,
  output S1024,
  output S512,
  output S256,
  output S128,
  output S64,
  output S32,
  output S16,
  output S8,
  output S4,
  output S2,
  output S1
);

  wire and_1_out, and_2_out, and_3_out, and_4_out, and_5_out, and_6_out, and_7_out, and_8_out, and_9_out,
       and_10_out, and_11_out, and_12_out, and_13_out, and_14_out, and_15_out, somador_completo_1_bit_2_val1,
       somador_completo_1_bit_3_val1, somador_completo_1_bit_4_val1, somador_completo_1_bit_5_val1,
       somador_completo_1_bit_6_val1, somador_completo_1_bit_7_val1, somador_completo_1_bit_8_val1,
       somador_completo_1_bit_9_val1, somador_completo_1_bit_10_val1, somador_completo_1_bit_11_val1,
       somador_completo_1_bit_12_val1, somador_completo_1_bit_13_val1, somador_completo_1_bit_14_val1;

  // AND_Gate and_1 has open pins: out=and_1_out
  somador_completo_1_bit somador_completo_1_bit_1 (
    .A(somador_completo_1_bit_2_val1), .B(and_1_out), .Val1(S32768), .Soma(S16384));  // open: Vem1
  // AND_Gate and_2 has open pins: out=and_2_out
  somador_completo_1_bit somador_completo_1_bit_2 (
    .A(somador_completo_1_bit_3_val1), .B(and_2_out), .Val1(somador_completo_1_bit_2_val1), .Soma(S8192));  // open: Vem1
  // AND_Gate and_3 has open pins: out=and_3_out
  somador_completo_1_bit somador_completo_1_bit_3 (
    .A(somador_completo_1_bit_4_val1), .B(and_3_out), .Val1(somador_completo_1_bit_3_val1), .Soma(S4096));  // open: Vem1
  // AND_Gate and_4 has open pins: out=and_4_out
  somador_completo_1_bit somador_completo_1_bit_4 (
    .A(somador_completo_1_bit_5_val1), .B(and_4_out), .Val1(somador_completo_1_bit_4_val1), .Soma(S2048));  // open: Vem1
  // AND_Gate and_5 has open pins: out=and_5_out
  somador_completo_1_bit somador_completo_1_bit_5 (
    .A(somador_completo_1_bit_6_val1), .B(and_5_out), .Val1(somador_completo_1_bit_5_val1), .Soma(S1024));  // open: Vem1
  // AND_Gate and_6 has open pins: out=and_6_out
  somador_completo_1_bit somador_completo_1_bit_6 (
    .A(somador_completo_1_bit_7_val1), .B(and_6_out), .Val1(somador_completo_1_bit_6_val1), .Soma(S512));  // open: Vem1
  // AND_Gate and_7 has open pins: out=and_7_out
  somador_completo_1_bit somador_completo_1_bit_7 (
    .A(somador_completo_1_bit_8_val1), .B(and_7_out), .Val1(somador_completo_1_bit_7_val1), .Soma(S256));  // open: Vem1
  // AND_Gate and_8 has open pins: out=and_8_out
  somador_completo_1_bit somador_completo_1_bit_8 (
    .A(somador_completo_1_bit_9_val1), .B(and_8_out), .Val1(somador_completo_1_bit_8_val1), .Soma(S128));  // open: Vem1
  // AND_Gate and_9 has open pins: out=and_9_out
  somador_completo_1_bit somador_completo_1_bit_9 (
    .A(somador_completo_1_bit_10_val1), .B(and_9_out), .Val1(somador_completo_1_bit_9_val1), .Soma(S64));  // open: Vem1
  // AND_Gate and_10 has open pins: out=and_10_out
  somador_completo_1_bit somador_completo_1_bit_10 (
    .A(somador_completo_1_bit_11_val1), .B(and_10_out), .Val1(somador_completo_1_bit_10_val1), .Soma(S32));  // open: Vem1
  // AND_Gate and_11 has open pins: out=and_11_out
  somador_completo_1_bit somador_completo_1_bit_11 (
    .A(somador_completo_1_bit_12_val1), .B(and_11_out), .Val1(somador_completo_1_bit_11_val1), .Soma(S16));  // open: Vem1
  // AND_Gate and_12 has open pins: out=and_12_out
  somador_completo_1_bit somador_completo_1_bit_12 (
    .A(somador_completo_1_bit_13_val1), .B(and_12_out), .Val1(somador_completo_1_bit_12_val1), .Soma(S8));  // open: Vem1
  // AND_Gate and_13 has open pins: out=and_13_out
  somador_completo_1_bit somador_completo_1_bit_13 (
    .A(somador_completo_1_bit_14_val1), .B(and_13_out), .Val1(somador_completo_1_bit_13_val1), .Soma(S4));  // open: Vem1
  // AND_Gate and_14 has open pins: out=and_14_out
  // AND_Gate and_15 has open pins: out=and_15_out
  somador_completo_1_bit somador_completo_1_bit_14 (
    .A(and_15_out), .B(and_14_out), .Val1(somador_completo_1_bit_14_val1), .Soma(S2));  // open: Vem1
  and and_16 (S1, B1, A1);
endmodule
